# Fritzing sketch menorah (saved by Fritzing 0.9.3b)
breadboards: 1

parts:
  Part1 = Arduino Uno (Rev3)
  LED1 = LED - 5mm [color="Blue (430nm)" current=20mA package="5 mm [THT]"]
  R1 = Resistor [tolerance=±5% resistance=100 package=THT]
  LED2 = LED - 5mm [color="White (4500K)" current=20mA package="5 mm [THT]"]
  R2 = Resistor [tolerance=±5% resistance=100 package=THT]
  R3 = Resistor [tolerance=±5% resistance=100 package=THT]
  R4 = Resistor [tolerance=±5% resistance=100 package=THT]
  R5 = Resistor [tolerance=±5% resistance=100 package=THT]
  R6 = Resistor [tolerance=±5% resistance=100 package=THT]
  R7 = Resistor [tolerance=±5% resistance=100 package=THT]
  R8 = Resistor [tolerance=±5% resistance=100 package=THT]
  R9 = Resistor [tolerance=±5% resistance=100 package=THT]
  LED3 = LED - 5mm [color="White (4500K)" current=20mA package="5 mm [THT]"]
  LED4 = LED - 5mm [color="White (4500K)" current=20mA package="5 mm [THT]"]
  LED5 = LED - 5mm [color="White (4500K)" current=20mA package="5 mm [THT]"]
  LED6 = LED - 5mm [color="White (4500K)" current=20mA package="5 mm [THT]"]
  LED7 = LED - 5mm [color="White (4500K)" current=20mA package="5 mm [THT]"]
  LED8 = LED - 5mm [color="White (4500K)" current=20mA package="5 mm [THT]"]
  LED9 = LED - 5mm [color="White (4500K)" current=20mA package="5 mm [THT]"]
  R10 = Resistor [tolerance=±5% resistance=100 package=THT]

nets:
  N1: Part1.A0, Part1.A1, Part1.A2, Part1.A5/SCL, R10.Pin_1
  N2: Part1.D8, R3.Pin_1
  N3: Part1.D9_PWM, R2.Pin_1
  N4: Part1.D13/SCK, R1.Pin_1
  N5: Part1.GND, LED1.cathode, LED2.cathode, LED3.cathode, LED4.cathode, LED5.cathode, LED6.cathode, LED7.cathode, LED8.cathode, LED9.cathode
  N6: Part1.D2, R9.Pin_1
  N7: Part1.D3_PWM, R8.Pin_1
  N8: Part1.D4, R7.Pin_1
  N9: Part1.D5_PWM, R6.Pin_1
  N10: Part1.D6_PWM, R5.Pin_1
  N11: Part1.D7, R4.Pin_1
  N12: Part1.5V, R10.Pin_0
  N13: LED1.anode, R1.Pin_0
  N14: LED2.anode, R2.Pin_0
  N15: R3.Pin_0, LED3.anode
  N16: R4.Pin_0, LED4.anode
  N17: R5.Pin_0, LED5.anode
  N18: R6.Pin_0, LED6.anode
  N19: R7.Pin_0, LED7.anode
  N20: R8.Pin_0, LED8.anode
  N21: R9.Pin_0, LED9.anode
